// Digital circuit divisor-4x4.dig as structural Verilog
module divisor_4x4 (
  input  [3:0] A,
  input  [3:0] B,
  output [3:0] Q,
  output [3:0] R
);

  wire [3:0] R1, R2, R3;

  divide_step divide_step_1 (.R_in(4'b0000), .A_in(A[3]), .B_in(B), .R_out(R1), .Q_out(Q[3]));
  divide_step divide_step_2 (.R_in(R2), .A_in(A[1]), .B_in(B), .R_out(R3), .Q_out(Q[1]));
  divide_step divide_step_3 (.R_in(R1), .A_in(A[2]), .B_in(B), .R_out(R2), .Q_out(Q[2]));
  divide_step divide_step_4 (.R_in(R3), .A_in(A[0]), .B_in(B), .R_out(R), .Q_out(Q[0]));

  // Other names for the same wires on the sheet: R_final[3:0] = R
endmodule
